// Logisim project Simple processor design.circ as structural Verilog: 18 circuits, main circuit CPU
module CPU (
  input  [7:0] in_1,
  input  in_2,
  input  [2:0] in_3,
  input  [7:0] MAR,
  input  in_5,
  input  in_6,
  input  in_7,
  input  in_8,
  output out_9,
  output out_10,
  output out_11,
  output [7:0] out_12,
  output [7:0] out_13
);

  wire clock_1_out, n3_8_decoder_free_1_out_2, n3_8_decoder_free_1_out_3, n3_8_decoder_free_1_out_4,
       n3_8_decoder_free_1_out_5, n3_8_decoder_free_1_out_6, n3_8_decoder_free_1_out_7,
       n3_8_decoder_free_1_out_8, n3_8_decoder_free_1_out_9;
  wire [7:0] controlled_buffer_1_out, controlled_buffer_2_out, ram_1_data, register_1_out_4, register_2_q,
       register_3_out_4, register_4_out_4;

  Clock clock_1 (.out(clock_1_out));
  assign controlled_buffer_1_out = in_2 ? ram_1_data : 8'bz;  // Controlled_Buffer controlled_buffer_1
  Register register_1 (.in_1(controlled_buffer_1_out), .in_2(in_2), .out_4(register_1_out_4), .in_3(1'b1));
  _3_8_decoder_free u_3_8_decoder_free_1 (
    .in_1(in_3), .out_2(n3_8_decoder_free_1_out_2), .out_3(n3_8_decoder_free_1_out_3),
    .out_4(n3_8_decoder_free_1_out_4), .out_5(n3_8_decoder_free_1_out_5), .out_6(n3_8_decoder_free_1_out_6),
    .out_7(n3_8_decoder_free_1_out_7), .out_8(n3_8_decoder_free_1_out_8), .out_9(n3_8_decoder_free_1_out_9));
  Alu alu_1 (
    .out_9(out_9), .out_10(out_11), .a(in_1), .x(out_12), .multi_15_8_bit(out_13), .b(register_1_out_4),
    .out_13(out_10), .sub(n3_8_decoder_free_1_out_2), .add(n3_8_decoder_free_1_out_3),
    .\and (n3_8_decoder_free_1_out_4), .\or (n3_8_decoder_free_1_out_5), .\xor (n3_8_decoder_free_1_out_6),
    .multi(n3_8_decoder_free_1_out_7));
  assign controlled_buffer_2_out = in_5 ? register_4_out_4 : 8'bz;  // Controlled_Buffer controlled_buffer_2
  Register_part register_2 (.D(controlled_buffer_2_out), .en(in_6), .Q(register_2_q), .clk(clock_1_out));  // open: clr
  Register register_3 (.in_1(MAR), .in_2(in_6), .out_4(register_3_out_4), .in_3(in_6));
  Register register_4 (.in_1(out_12), .in_2(in_8), .out_4(register_4_out_4), .in_3(in_6));
  RAM #(.bus("separate")) ram_1 (
    .addr(register_3_out_4), .din(register_2_q), .data(ram_1_data), .str(n3_8_decoder_free_1_out_9),
    .sel(in_7), .clk(clock_1_out), .ld(n3_8_decoder_free_1_out_8));  // open: clr

  // Notes on the sheet:
  //   op code
  //   000 sub
  //   001 add
  //   010 and
  //   011 or
  //   100 xor
  //   101 mul
  //   110 ld
  //   111 str
  //   MBR
  //   ld
  //   str
  //   RAM
  //   Data bus
endmodule

module Alu (
  input  [7:0] a,
  input  [7:0] b,
  input  sub,
  input  add,
  input  \and ,
  input  \or ,
  input  \xor ,
  input  multi,
  output out_9,
  output out_10,
  output [7:0] x,
  output [7:0] multi_15_8_bit,
  output out_13
);

  wire n8bitadder_1_out_4, or_2_out;
  wire [7:0] and_1_out, bit_extender_1_out, multiplication_8_bit_1_out_4, n8bitadder_1_out_5, or_1_out,
       xor_1_out, xor_2_out;

  assign bit_extender_1_out = {{7{sub}}, sub};  // Bit_Extender bit_extender_1
  multiplication_8_bit multiplication_8_bit_1 (
    .in_1(b), .out_3(multi_15_8_bit), .out_4(multiplication_8_bit_1_out_4));  // open: in_2
  assign xor_1_out = a ^ b;  // XOR_Gate xor_1, 8 bits wide
  assign or_1_out = a | b;  // OR_Gate or_1, 8 bits wide
  assign and_1_out = a & b;  // AND_Gate and_1, 8 bits wide
  assign xor_2_out = b ^ bit_extender_1_out;  // XOR_Gate xor_2, 8 bits wide
  _8bitadder u_8bitadder_1 (
    .in_1(a), .in_2(xor_2_out), .in_3(sub), .out_4(n8bitadder_1_out_4), .out_5(n8bitadder_1_out_5));
  or or_2 (or_2_out, sub, add);
  assign out_13 = or_2_out ? n8bitadder_1_out_4 : 1'bz;  // Controlled_Buffer controlled_buffer_1
  assign {out_10, x[6:0]} = \or  ? or_1_out : 8'bz;  // Controlled_Buffer controlled_buffer_2
  assign {out_10, x[6:0]} = \and  ? and_1_out : 8'bz;  // Controlled_Buffer controlled_buffer_3
  assign {out_10, x[6:0]} = or_2_out ? n8bitadder_1_out_5 : 8'bz;  // Controlled_Buffer controlled_buffer_4
  assign {out_10, x[6:0]} = multi ? multiplication_8_bit_1_out_4 : 8'bz;  // Controlled_Buffer controlled_buffer_5
  assign {out_10, x[6:0]} = \xor  ? xor_1_out : 8'bz;  // Controlled_Buffer controlled_buffer_6
  nor nor_1 (out_9, x[0], x[1], x[2], x[3], x[5], x[6], out_10, x[4]);

  assign x[7] = out_10;
endmodule

module Register (
  input  [7:0] in_1,
  input  in_2,
  input  in_3,
  output [7:0] out_4
);

  wire [7:0] d_flipflop_1_out_3;

  D_flipflop d_flipflop_1 (.in_1(in_1[0]), .out_3(d_flipflop_1_out_3[0]), .in_2(in_2));
  D_flipflop d_flipflop_2 (.in_1(in_1[1]), .out_3(d_flipflop_1_out_3[1]), .in_2(in_2));
  D_flipflop d_flipflop_3 (.in_1(in_1[2]), .out_3(d_flipflop_1_out_3[2]), .in_2(in_2));
  D_flipflop d_flipflop_4 (.in_1(in_1[3]), .out_3(d_flipflop_1_out_3[3]), .in_2(in_2));
  D_flipflop d_flipflop_5 (.in_1(in_1[4]), .out_3(d_flipflop_1_out_3[4]), .in_2(in_2));
  D_flipflop d_flipflop_6 (.in_1(in_1[5]), .out_3(d_flipflop_1_out_3[5]), .in_2(in_2));
  D_flipflop d_flipflop_7 (.in_1(in_1[6]), .out_3(d_flipflop_1_out_3[6]), .in_2(in_2));
  D_flipflop d_flipflop_8 (.in_1(in_1[7]), .out_3(d_flipflop_1_out_3[7]), .in_2(in_2));
  assign out_4 = in_3 ? d_flipflop_1_out_3 : 8'bz;  // Controlled_Buffer controlled_buffer_1
endmodule

module _3_8_decoder_free (
  input  [2:0] in_1,
  output out_2,
  output out_3,
  output out_4,
  output out_5,
  output out_6,
  output out_7,
  output out_8,
  output out_9
);

  wire not_1_out, not_2_out, not_3_out;

  not not_1 (not_1_out, in_1[0]);
  not not_2 (not_2_out, in_1[1]);
  not not_3 (not_3_out, in_1[2]);
  and and_1 (out_2, not_1_out, not_2_out, not_3_out);
  and and_2 (out_3, in_1[0], not_2_out, not_3_out);
  and and_3 (out_4, not_1_out, in_1[1], not_3_out);
  and and_4 (out_5, in_1[0], in_1[1], not_3_out);
  and and_5 (out_6, not_1_out, not_2_out, in_1[2]);
  and and_6 (out_7, in_1[0], not_2_out, in_1[2]);
  and and_7 (out_8, not_1_out, in_1[1], in_1[2]);
  and and_8 (out_9, in_1[0], in_1[1], in_1[2]);
endmodule

module _8bitadder (
  input  [7:0] in_1,
  input  [7:0] in_2,
  input  in_3,
  output out_4,
  output [7:0] out_5
);

  wire n4bitadder_2_out_4;

  _4bitadder u_4bitadder_1 (
    .in_1(in_1[7:4]), .in_2(in_2[7:4]), .in_3(n4bitadder_2_out_4), .out_4(out_4), .out_5(out_5[7:4]));
  _4bitadder u_4bitadder_2 (
    .in_1(in_1[3:0]), .in_2(in_2[3:0]), .in_3(in_3), .out_4(n4bitadder_2_out_4), .out_5(out_5[3:0]));
endmodule

module _4bitadder (
  input  [3:0] in_1,
  input  [3:0] in_2,
  input  in_3,
  output out_4,
  output [3:0] out_5
);

  wire full_adder_2_out_5, full_adder_3_out_5, full_adder_4_out_5;

  Full_Adder full_adder_1 (.in_1(in_1[3]), .in_2(in_2[3]), .in_3(full_adder_2_out_5), .out_4(out_5[3]), .out_5(out_4));
  Full_Adder full_adder_2 (
    .in_1(in_1[2]), .in_2(in_2[2]), .in_3(full_adder_3_out_5), .out_4(out_5[2]), .out_5(full_adder_2_out_5));
  Full_Adder full_adder_3 (
    .in_1(in_1[1]), .in_2(in_2[1]), .in_3(full_adder_4_out_5), .out_4(out_5[1]), .out_5(full_adder_3_out_5));
  Full_Adder full_adder_4 (.in_1(in_1[0]), .in_2(in_2[0]), .in_3(in_3), .out_4(out_5[0]), .out_5(full_adder_4_out_5));
endmodule

module multiplication_8_bit (
  input  [7:0] in_1,
  input  [7:0] in_2,
  output [7:0] out_3,
  output [7:0] out_4
);

  wire [7:0] multiplication_1_bit_1_out_5, multiplication_1_bit_2_out_5, multiplication_1_bit_3_out_5,
       multiplication_1_bit_4_out_5, multiplication_1_bit_5_out_5, multiplication_1_bit_6_out_5,
       multiplication_1_bit_7_out_5;

  multiplication_1_bit multiplication_1_bit_1 (
    .in_1(in_1[0]), .in_2(in_2), .in_3({8{1'b0}}), .out_4(out_4[0]), .out_5(multiplication_1_bit_1_out_5));
  multiplication_1_bit multiplication_1_bit_2 (
    .in_1(in_1[1]), .in_2(in_2), .in_3(multiplication_1_bit_1_out_5), .out_4(out_4[1]),
    .out_5(multiplication_1_bit_2_out_5));
  multiplication_1_bit multiplication_1_bit_3 (
    .in_1(in_1[2]), .in_2(in_2), .in_3(multiplication_1_bit_2_out_5), .out_4(out_4[2]),
    .out_5(multiplication_1_bit_3_out_5));
  multiplication_1_bit multiplication_1_bit_4 (
    .in_1(in_1[3]), .in_2(in_2), .in_3(multiplication_1_bit_3_out_5), .out_4(out_4[3]),
    .out_5(multiplication_1_bit_4_out_5));
  multiplication_1_bit multiplication_1_bit_5 (
    .in_1(in_1[4]), .in_2(in_2), .in_3(multiplication_1_bit_4_out_5), .out_4(out_4[4]),
    .out_5(multiplication_1_bit_5_out_5));
  multiplication_1_bit multiplication_1_bit_6 (
    .in_1(in_1[6]), .in_2(in_2), .in_3(multiplication_1_bit_7_out_5), .out_4(out_4[6]),
    .out_5(multiplication_1_bit_6_out_5));
  multiplication_1_bit multiplication_1_bit_7 (
    .in_1(in_1[5]), .in_2(in_2), .in_3(multiplication_1_bit_5_out_5), .out_4(out_4[5]),
    .out_5(multiplication_1_bit_7_out_5));
  multiplication_1_bit multiplication_1_bit_8 (
    .in_1(in_1[7]), .in_2(in_2), .in_3(multiplication_1_bit_6_out_5), .out_4(out_4[7]), .out_5(out_3));

  // Notes on the sheet:
  //   in_1: pull=up
  //   out_4: pull=up
endmodule

module multiplication_1_bit (
  input  in_1,
  input  [7:0] in_2,
  input  [7:0] in_3,
  output out_4,
  output [7:0] out_5
);

  wire [7:0] and_1_out;

  and and_1 (and_1_out[0], in_1, in_2[0]);
  and and_2 (and_1_out[1], in_1, in_2[1]);
  and and_3 (and_1_out[2], in_1, in_2[2]);
  and and_4 (and_1_out[3], in_1, in_2[3]);
  and and_5 (and_1_out[4], in_1, in_2[4]);
  and and_6 (and_1_out[5], in_1, in_2[5]);
  and and_7 (and_1_out[6], in_1, in_2[6]);
  and and_8 (and_1_out[7], in_1, in_2[7]);
  Adder adder_1 (.a(and_1_out), .b(in_3), .out({out_5[6:0], out_4}));  // open: cin, cout

  assign out_5[7] = 1'b0;
endmodule

module Multiplexerx_8_1_8_bit (
  input  [7:0] in_1,
  input  [7:0] in_2,
  input  [7:0] in_3,
  input  [7:0] in_4,
  input  [7:0] in_5,
  input  [7:0] in_6,
  input  [7:0] in_7,
  input  [7:0] in_8,
  input  [2:0] in_9,
  output [7:0] out_10
);

  multiplexer_8_1 multiplexer_8_1_1 (
    .in_1(in_1[0]), .in_2(in_2[0]), .in_3(in_3[0]), .in_4(in_4[0]), .in_5(in_5[0]), .in_6(in_6[0]),
    .in_7(in_7[0]), .in_8(in_8[0]), .in_9(in_9), .out_10(out_10[0]));
  multiplexer_8_1 multiplexer_8_1_2 (
    .in_1(in_1[1]), .in_2(in_2[1]), .in_3(in_3[1]), .in_4(in_4[1]), .in_5(in_5[1]), .in_6(in_6[1]),
    .in_7(in_7[1]), .in_8(in_8[1]), .in_9(in_9), .out_10(out_10[1]));
  multiplexer_8_1 multiplexer_8_1_3 (
    .in_1(in_1[2]), .in_2(in_2[2]), .in_3(in_3[2]), .in_4(in_4[2]), .in_5(in_5[2]), .in_6(in_6[2]),
    .in_7(in_7[2]), .in_8(in_8[2]), .in_9(in_9), .out_10(out_10[2]));
  multiplexer_8_1 multiplexer_8_1_4 (
    .in_1(in_1[3]), .in_2(in_2[3]), .in_3(in_3[3]), .in_4(in_4[3]), .in_5(in_5[3]), .in_6(in_6[3]),
    .in_7(in_7[3]), .in_8(in_8[3]), .in_9(in_9), .out_10(out_10[3]));
  multiplexer_8_1 multiplexer_8_1_5 (
    .in_1(in_1[4]), .in_2(in_2[4]), .in_3(in_3[4]), .in_4(in_4[4]), .in_5(in_5[4]), .in_6(in_6[4]),
    .in_7(in_7[4]), .in_8(in_8[4]), .in_9(in_9), .out_10(out_10[4]));
  multiplexer_8_1 multiplexer_8_1_6 (
    .in_1(in_1[5]), .in_2(in_2[5]), .in_3(in_3[5]), .in_4(in_4[5]), .in_5(in_5[5]), .in_6(in_6[5]),
    .in_7(in_7[5]), .in_8(in_8[5]), .in_9(in_9), .out_10(out_10[5]));
  multiplexer_8_1 multiplexer_8_1_7 (
    .in_1(in_1[6]), .in_2(in_2[6]), .in_3(in_3[6]), .in_4(in_4[6]), .in_5(in_5[6]), .in_6(in_6[6]),
    .in_7(in_7[6]), .in_8(in_8[6]), .in_9(in_9), .out_10(out_10[6]));
  multiplexer_8_1 multiplexer_8_1_8 (
    .in_1(in_1[7]), .in_2(in_2[7]), .in_3(in_2[7]), .in_4(in_4[7]), .in_5(in_5[7]), .in_6(in_6[7]),
    .in_7(in_7[7]), .in_8(in_8[7]), .in_9(in_9), .out_10(out_10[7]));

  assign in_3[7] = in_2[7];
endmodule

module multiplexer_8_1 (
  input  in_1,
  input  in_2,
  input  in_3,
  input  in_4,
  input  in_5,
  input  in_6,
  input  in_7,
  input  in_8,
  input  [2:0] in_9,
  output out_10
);

  wire and_1_out, and_2_out, and_3_out, and_4_out, and_5_out, and_6_out, and_7_out, and_8_out, not_1_out,
       not_2_out, not_3_out;

  not not_1 (not_1_out, in_9[2]);
  not not_2 (not_2_out, in_9[1]);
  not not_3 (not_3_out, in_9[0]);
  and and_1 (and_1_out, in_1, not_1_out, not_2_out, not_3_out);
  and and_2 (and_2_out, in_2, not_1_out, not_2_out, in_9[0]);
  and and_3 (and_3_out, in_3, not_1_out, in_9[1], not_3_out);
  and and_4 (and_4_out, in_4, not_1_out, in_9[1], in_9[0]);
  and and_5 (and_5_out, in_5, in_9[2], not_2_out, not_3_out);
  and and_6 (and_6_out, in_9[2], in_6, not_2_out, in_9[0]);
  and and_7 (and_7_out, in_7, in_9[2], in_9[1], not_3_out);
  and and_8 (and_8_out, in_8, in_9[2], in_9[1], in_9[0]);
  or or_1 (out_10, and_1_out, and_2_out, and_3_out, and_4_out, and_5_out, and_6_out, and_7_out, and_8_out);
endmodule

module D_flipflop (
  input  in_1,
  input  in_2,
  output out_3
);

  wire nand_1_out, nand_2_out, nand_4_out, not_1_out;

  not not_1 (not_1_out, in_1);
  nand nand_1 (nand_1_out, in_1, in_2);
  nand nand_2 (nand_2_out, not_1_out, in_2);
  nand nand_3 (out_3, nand_1_out, nand_4_out);
  nand nand_4 (nand_4_out, out_3, nand_2_out);
endmodule

module Bindec (
  input  in_1,
  input  in_2,
  input  in_3,
  output out_4,
  output out_5,
  output out_6,
  output out_7
);

  and and_1 (out_4, ~in_1, in_3, ~in_2);  // AND_Gate
  and and_2 (out_5, in_1, in_3, ~in_2);  // AND_Gate
  and and_3 (out_6, ~in_1, in_3, in_2);  // AND_Gate
  and and_4 (out_7, in_1, in_3, in_2);
endmodule

module Full_Adder (
  input  in_1,
  input  in_2,
  input  in_3,
  output out_4,
  output out_5
);

  wire and_1_out, and_2_out, xor_1_out;

  and and_1 (and_1_out, in_2, in_1);
  xor xor_1 (xor_1_out, in_1, in_2);
  xor xor_2 (out_4, xor_1_out, in_3);
  and and_2 (and_2_out, in_3, xor_1_out);
  or or_1 (out_5, and_2_out, and_1_out);
endmodule

module _3_8_decoder (
  input  [2:0] in_1,
  input  in_2,
  output out_3,
  output out_4,
  output out_5,
  output out_6,
  output out_7,
  output out_8,
  output out_9,
  output out_10
);

  wire not_1_out, not_2_out, not_3_out;

  not not_1 (not_1_out, in_1[0]);
  not not_2 (not_2_out, in_1[1]);
  not not_3 (not_3_out, in_1[2]);
  and and_1 (out_3, not_1_out, not_2_out, not_3_out, in_2);
  and and_2 (out_4, in_1[0], not_2_out, not_3_out, in_2);
  and and_3 (out_5, not_1_out, in_1[1], not_3_out, in_2);
  and and_4 (out_6, in_1[0], in_1[1], not_3_out, in_2);
  and and_5 (out_7, not_1_out, not_2_out, in_1[2], in_2);
  and and_6 (out_8, in_1[0], not_2_out, in_1[2], in_2);
  and and_7 (out_9, not_1_out, in_1[1], in_1[2], in_2);
  and and_8 (out_10, in_1[0], in_1[1], in_1[2], in_2);
endmodule

module Leftshifter (
  input  [7:0] in_1,
  output [7:0] out_2,
  output out_3
);


  assign out_2 = {in_1[6:0], 1'b0};
  assign out_3 = in_1[7];
endmodule

module Rightshifter (
  input  [7:0] in_1,
  output out_2,
  output [7:0] out_3
);


  assign out_2 = in_1[0];
  assign out_3 = {1'b0, in_1[7:1]};
endmodule

module Computer (
);

  wire alu_1_p4, alu_1_p8, alu_1_p11, and_1_out, and_2_out, and_3_out, and_4_out, and_5_out, and_6_out,
       and_7_out, and_8_out, and_9_out, and_10_out, and_11_out, and_12_out, and_13_out, and_14_out,
       and_15_out, and_16_out, and_17_out, and_18_out, and_19_out, and_20_out, and_21_out, and_22_out,
       and_23_out, buffer_1_out, button_1_out, clock_1_out, controlled_buffer_3_out, d_ff_1_q, d_ff_2_q,
       d_ff_4_q, n3_8_decoder_free_1_out_2, n3_8_decoder_free_1_out_3, n3_8_decoder_free_1_out_4,
       n3_8_decoder_free_1_out_5, n3_8_decoder_free_1_out_6, n3_8_decoder_free_1_out_7,
       n3_8_decoder_free_1_out_8, not_1_out, or_1_out, xnor_1_out, xnor_2_out, xnor_3_out, xor_1_out,
       xor_2_out;
  wire [0:0] not_2_out, not_3_out, not_4_out, not_5_out, not_7_out, register_3_q_2;
  wire [2:0] controlled_buffer_1_out_2, controlled_buffer_1_out_3, d_ff_3_q;
  wire [7:0] alu_1_p13, controlled_buffer_10_out, counter_1_q, multiplexerx_8_1_8_bit_1_out_10,
       multiplexerx_8_1_8_bit_2_out_10, multiplexerx_8_1_8_bit_3_out_10, register_1_q, register_2_q;
  wire [7:2] register_3_q_3;
  wire [16:15] or_2_out;
  wire [17:17] register_3_q;
  wire [20:0] controlled_buffer_1_out;

  Clock clock_1 (.out(clock_1_out));
  Button button_1 (.out(button_1_out));
  D_Flip_Flop #(.trigger("falling")) d_ff_1 (
    .clk(button_1_out), .D(clock_1_out), .Q(d_ff_1_q));  // open: Qn, preset, en, reset
  xnor xnor_1 (xnor_1_out, d_ff_1_q, clock_1_out);
  Register_part register_1 (
    .D(alu_1_p13), .en(controlled_buffer_1_out[0]), .Q(register_1_q), .clk(xnor_1_out), .clr(button_1_out));
  Register_part register_2 (
    .D(alu_1_p13), .en(controlled_buffer_1_out[1]), .Q(register_2_q), .clk(xnor_1_out), .clr(button_1_out));
  // Probe on {controlled_buffer_1_out[20], controlled_buffer_1_out_3, controlled_buffer_1_out[16:14], controlled_buffer_1_out_2, controlled_buffer_1_out[10:0]}
  Multiplexerx_8_1_8_bit multiplexerx_8_1_8_bit_1 (
    .in_1(register_1_q), .in_2(register_2_q), .in_3(controlled_buffer_10_out),
    .in_9(controlled_buffer_1_out[7:5]), .out_10(multiplexerx_8_1_8_bit_1_out_10));  // open: in_4, in_5, in_6, in_7, in_8
  Multiplexerx_8_1_8_bit multiplexerx_8_1_8_bit_2 (
    .in_1(register_1_q), .in_2(register_2_q), .in_3({8{1'b0}}), .in_4(controlled_buffer_10_out),
    .in_9(controlled_buffer_1_out[4:2]), .out_10(multiplexerx_8_1_8_bit_2_out_10));  // open: in_5, in_6, in_7, in_8
  and and_1 (and_1_out, xnor_1_out, d_ff_2_q);
  assign {controlled_buffer_1_out[20], controlled_buffer_1_out_3, controlled_buffer_1_out[16:14], controlled_buffer_1_out_2, controlled_buffer_1_out[10:0]} = and_1_out ? 21'h150000 : 21'bz;  // Controlled_Buffer controlled_buffer_1
  D_Flip_Flop d_ff_2 (
    .clk(xnor_1_out), .D(controlled_buffer_3_out), .Q(d_ff_2_q), .preset(button_1_out));  // open: Qn, en, reset
  not not_1 (not_1_out, and_1_out);
  and and_2 (and_2_out, and_3_out, ~xnor_2_out);  // AND_Gate
  assign {controlled_buffer_1_out[20], controlled_buffer_1_out_3, controlled_buffer_1_out[16:14], controlled_buffer_1_out_2, controlled_buffer_1_out[10:0]} = and_2_out ? {15'h5404, register_3_q_2[0], 3'b010, register_3_q[17], not_2_out[0]} : 21'bz;  // Controlled_Buffer controlled_buffer_2
  and and_3 (and_3_out, and_8_out, not_1_out);
  assign controlled_buffer_3_out = and_2_out ? 1'b1 : 1'bz;  // Controlled_Buffer controlled_buffer_3
  and and_4 (and_4_out, and_9_out, not_1_out);
  and and_5 (and_5_out, and_10_out, not_1_out);
  not not_2 (not_2_out[0], register_3_q[17]);
  assign {controlled_buffer_1_out[20], controlled_buffer_1_out_3, controlled_buffer_1_out[16:14], controlled_buffer_1_out_2, controlled_buffer_1_out[10:0]} = and_4_out ? {3'b000, register_3_q[17], 11'h104, register_3_q_2[0], 5'b01000} : 21'bz;  // Controlled_Buffer controlled_buffer_4
  not not_3 (not_3_out[0], register_3_q[17]);
  assign {controlled_buffer_1_out[20], controlled_buffer_1_out_3, controlled_buffer_1_out[16:14], controlled_buffer_1_out_2, controlled_buffer_1_out[10:0]} = and_5_out ? {3'b100, register_3_q_2[0], 15'h52, register_3_q[17], not_3_out[0]} : 21'bz;  // Controlled_Buffer controlled_buffer_5
  // Probe on multiplexerx_8_1_8_bit_1_out_10
  // Probe on multiplexerx_8_1_8_bit_2_out_10
  assign controlled_buffer_3_out = and_4_out ? 1'b1 : 1'bz;  // Controlled_Buffer controlled_buffer_6
  assign controlled_buffer_3_out = and_5_out ? 1'b1 : 1'bz;  // Controlled_Buffer controlled_buffer_7
  _3_8_decoder_free u_3_8_decoder_free_1 (
    .in_1(controlled_buffer_1_out[10:8]), .out_2(n3_8_decoder_free_1_out_2),
    .out_3(n3_8_decoder_free_1_out_3), .out_4(n3_8_decoder_free_1_out_4), .out_5(n3_8_decoder_free_1_out_5),
    .out_6(n3_8_decoder_free_1_out_6), .out_7(n3_8_decoder_free_1_out_7), .out_8(n3_8_decoder_free_1_out_8));  // open: out_9
  xor xor_1 (xor_1_out, xnor_1_out, buffer_1_out);
  buf buffer_1 (buffer_1_out, xnor_1_out);
  and and_6 (and_6_out, d_ff_2_q, ~controlled_buffer_3_out);  // AND_Gate
  xnor xnor_2 (xnor_2_out, register_3_q[17], register_3_q_2[0]);
  and and_7 (and_7_out, and_3_out, xnor_2_out);
  assign {controlled_buffer_1_out[20], controlled_buffer_1_out_3, controlled_buffer_1_out[16:14], controlled_buffer_1_out_2, controlled_buffer_1_out[10:0]} = and_7_out ? {19'h54052, register_3_q[17], not_4_out[0]} : 21'bz;  // Controlled_Buffer controlled_buffer_8
  Counter counter_1 (
    .load(controlled_buffer_1_out[15]), .D(alu_1_p13), .count(controlled_buffer_1_out[16]), .Q(counter_1_q),
    .clk(xor_1_out), .clr(button_1_out));  // open: carry
  assign controlled_buffer_3_out = and_7_out ? 1'b1 : 1'bz;  // Controlled_Buffer controlled_buffer_9
  // Probe on controlled_buffer_1_out_3
  not not_4 (not_4_out[0], register_3_q[17]);
  D_Flip_Flop d_ff_3 (
    .clk(xnor_1_out), .D(alu_1_p4), .Q(d_ff_3_q[0]), .en(controlled_buffer_1_out_2[2]), .reset(button_1_out));  // open: Qn, preset
  // Alu alu_1: pin names not known; wires that end beside it: multiplexerx_8_1_8_bit_1_out_10, multiplexerx_8_1_8_bit_2_out_10, n3_8_decoder_free_1_out_2, alu_1_p4, n3_8_decoder_free_1_out_3, n3_8_decoder_free_1_out_4, n3_8_decoder_free_1_out_5, alu_1_p8, n3_8_decoder_free_1_out_6, n3_8_decoder_free_1_out_7, alu_1_p11, n3_8_decoder_free_1_out_8, alu_1_p13
  Multiplexerx_8_1_8_bit multiplexerx_8_1_8_bit_3 (
    .in_1(register_1_q), .in_2(register_2_q), .in_3(counter_1_q), .in_9(controlled_buffer_1_out_3),
    .out_10(multiplexerx_8_1_8_bit_3_out_10));  // open: in_4, in_5, in_6, in_7, in_8
  D_Flip_Flop d_ff_4 (.clk(xnor_1_out), .D(and_6_out), .Q(d_ff_4_q), .reset(button_1_out));  // open: Qn, preset, en
  // Probe on alu_1_p13
  D_Flip_Flop d_ff_5 (
    .clk(xnor_1_out), .D(alu_1_p8), .Q(d_ff_3_q[1]), .en(controlled_buffer_1_out_2[1]), .reset(button_1_out));  // open: Qn, preset
  assign controlled_buffer_10_out = controlled_buffer_1_out[14] ? alu_1_p13 : 8'bz;  // Controlled_Buffer controlled_buffer_10
  D_Flip_Flop d_ff_6 (
    .clk(xnor_1_out), .D(alu_1_p11), .Q(d_ff_3_q[2]), .en(controlled_buffer_1_out_2[0]), .reset(button_1_out));  // open: Qn, preset
  RAM ram_1 (
    .addr(multiplexerx_8_1_8_bit_3_out_10), .data(controlled_buffer_10_out), .sel(1'b1), .clk(xnor_1_out),
    .ld(controlled_buffer_1_out[20]));  // open: clr
  Register_part #(.trigger("falling")) register_3 (
    .D(controlled_buffer_10_out), .en(d_ff_2_q), .Q({register_3_q_3, register_3_q[17], register_3_q_2[0]}),
    .clk(xnor_1_out));  // open: clr
  and and_8 (and_8_out, ~register_3_q_3[2], ~register_3_q_3[3], ~register_3_q_3[4], ~register_3_q_3[5], ~register_3_q_3[6], ~register_3_q_3[7]);  // AND_Gate
  and and_9 (and_9_out, ~register_3_q_3[2], register_3_q_3[3], ~register_3_q_3[4], ~register_3_q_3[5], ~register_3_q_3[6], ~register_3_q_3[7]);  // AND_Gate
  and and_10 (and_10_out, register_3_q_3[2], ~register_3_q_3[3], ~register_3_q_3[4], ~register_3_q_3[5], ~register_3_q_3[6], ~register_3_q_3[7]);  // AND_Gate
  and and_11 (and_11_out, and_22_out, not_1_out);
  and and_12 (and_12_out, and_23_out, not_1_out);
  assign controlled_buffer_3_out = and_11_out ? 1'b1 : 1'bz;  // Controlled_Buffer controlled_buffer_11
  and and_13 (and_13_out, and_12_out, ~xnor_3_out);  // AND_Gate
  assign {controlled_buffer_1_out[20], controlled_buffer_1_out_3, controlled_buffer_1_out[16:14], controlled_buffer_1_out_2, controlled_buffer_1_out[10:0]} = and_13_out ? {12'ha1c, register_3_q_3[3], 2'b00, register_3_q[17], 2'b00, register_3_q_2[0], register_3_q[17], not_5_out[0]} : 21'bz;  // Controlled_Buffer controlled_buffer_12
  assign {controlled_buffer_1_out[20], controlled_buffer_1_out_3, controlled_buffer_1_out[16:14], controlled_buffer_1_out_2, controlled_buffer_1_out[10:0]} = and_11_out ? {4'b1010, or_2_out, 15'h148} : 21'bz;  // Controlled_Buffer controlled_buffer_13
  not not_5 (not_5_out[0], register_3_q[17]);
  assign controlled_buffer_3_out = and_12_out ? 1'b1 : 1'bz;  // Controlled_Buffer controlled_buffer_14
  and and_14 (and_14_out, register_3_q[17], ~register_3_q_2[0]);  // AND_Gate
  and and_15 (and_15_out, d_ff_3_q[1], ~d_ff_3_q[0], and_17_out);  // AND_Gate
  and and_16 (and_16_out, ~d_ff_3_q[1], and_14_out);  // AND_Gate
  or or_1 (or_1_out, and_16_out, and_15_out, and_19_out);
  xor xor_2 (xor_2_out, register_3_q_3[2], or_1_out);
  or or_2 (or_2_out[15], xor_2_out, and_20_out);
  not not_6 (or_2_out[16], or_2_out[15]);
  and and_17 (and_17_out, ~register_3_q[17], register_3_q_2[0]);  // AND_Gate
  and and_18 (and_18_out, ~register_3_q[17], ~register_3_q_2[0]);  // AND_Gate
  and and_19 (and_19_out, d_ff_3_q[0], and_18_out);
  and and_20 (and_20_out, ~register_3_q_3[2], register_3_q[17], register_3_q_2[0]);  // AND_Gate
  xnor xnor_3 (xnor_3_out, register_3_q[17], register_3_q_2[0]);
  and and_21 (and_21_out, xnor_3_out, and_12_out);
  assign {controlled_buffer_1_out[20], controlled_buffer_1_out_3, controlled_buffer_1_out[16:14], controlled_buffer_1_out_2, controlled_buffer_1_out[10:0]} = and_21_out ? {12'ha9c, register_3_q_3[3], 2'b00, register_3_q[17], 3'b011, register_3_q[17], not_7_out[0]} : 21'bz;  // Controlled_Buffer controlled_buffer_15
  not not_7 (not_7_out[0], register_3_q[17]);
  and and_22 (and_22_out, ~register_3_q_3[3], ~register_3_q_3[4], register_3_q_3[5], ~register_3_q_3[6], ~register_3_q_3[7]);  // AND_Gate
  and and_23 (and_23_out, register_3_q_3[4], ~register_3_q_3[5], ~register_3_q_3[6], ~register_3_q_3[7]);  // AND_Gate

  // Notes on the sheet:
  //   clr
  //   clk
  //   a
  //   b
  //   clk
  //   ALU ctrl
  //   phase reset
  //   phase 1
  //   F-bus
  //   mov r,r / mov r,imm
  //   mov [r],r
  //   mov r,[r]
  //   Central Processing Unit
  //   ip
  //   A-sel
  //   z
  //   phase 2
  //   c
  //   A-Bus
  //   s
  //   D-bus
  //   add/sub r,r
  //   jb
  //   je
  //   ja
  //   jmp
  //   add/sub r,imm
endmodule

module Multiplexer2 (
  input  in_1,
  input  in_2,
  input  in_3,
  output out_4
);

  wire and_1_out, and_2_out, not_1_out;

  not not_1 (not_1_out, in_3);
  and and_1 (and_1_out, in_1, not_1_out);
  and and_2 (and_2_out, in_2, in_3);
  or or_1 (out_4, and_1_out, and_2_out);
endmodule
