// Logisim project comparq.circ as structural Verilog: 18 circuits, main circuit 8-bit adder
module full_adder (
  input  A,
  input  B,
  input  Ci,
  output S,
  output Co
);

  wire and_1_out, and_2_out, xor_1_out;

  xor xor_1 (xor_1_out, A, B);
  and and_1 (and_1_out, A, B);
  xor xor_2 (S, xor_1_out, Ci);
  and and_2 (and_2_out, xor_1_out, Ci);
  or or_1 (Co, and_2_out, and_1_out);

  // Notes on the sheet:
  //   Full Adder
endmodule

module _8_bit_adder (
  input  [7:0] Q1,
  input  [7:0] Q0,
  output [7:0] S,
  output O
);

  wire full_adder_1_co, full_adder_2_co, full_adder_3_co, full_adder_4_co, full_adder_5_co, full_adder_6_co,
       full_adder_7_co;

  full_adder full_adder_1 (.A(Q1[0]), .B(Q0[0]), .Ci(1'b0), .S(S[0]), .Co(full_adder_1_co));
  full_adder full_adder_2 (.A(Q1[1]), .B(Q0[1]), .Ci(full_adder_1_co), .S(S[1]), .Co(full_adder_2_co));
  full_adder full_adder_3 (.A(Q1[2]), .B(Q0[2]), .Ci(full_adder_2_co), .S(S[2]), .Co(full_adder_3_co));
  full_adder full_adder_4 (.A(Q1[3]), .B(Q0[3]), .Ci(full_adder_3_co), .S(S[3]), .Co(full_adder_4_co));
  full_adder full_adder_5 (.A(Q1[4]), .B(Q0[4]), .Ci(full_adder_4_co), .S(S[4]), .Co(full_adder_5_co));
  full_adder full_adder_6 (.A(Q1[5]), .B(Q0[5]), .Ci(full_adder_5_co), .S(S[5]), .Co(full_adder_6_co));
  full_adder full_adder_7 (.A(Q1[6]), .B(Q0[6]), .Ci(full_adder_6_co), .S(S[6]), .Co(full_adder_7_co));
  full_adder full_adder_8 (.A(Q1[7]), .B(Q0[7]), .Ci(full_adder_7_co), .S(S[7]), .Co(O));
endmodule

module D_flip_flop (
  input  D,
  input  C,
  output Q,
  output nQ
);

  wire nand_1_out, nand_2_out, not_1_out;

  not not_1 (not_1_out, D);
  nand nand_1 (nand_1_out, D, C);
  nand nand_2 (nand_2_out, C, not_1_out);
  nand nand_3 (Q, nand_1_out, nQ);
  nand nand_4 (nQ, Q, nand_2_out);

  // Notes on the sheet:
  //   D flip flop
endmodule

module test_Counter (
  input  Count,
  input  Clock,
  output Q0,
  output Q1,
  output Q2,
  output Q3,
  output Q4,
  output Q5,
  output Q7,
  output Q7_2
);

  wire and_1_out, and_2_out, and_3_out, and_4_out, and_5_out, and_6_out, and_7_out;

  and and_1 (and_1_out, Q0, Count);
  J_K_Flip_Flop j_k_ff_1 (.J(Count), .clk(Clock), .K(Count), .Q(Q0));  // open: Qn, preset, en, reset
  and and_2 (and_2_out, Q1, and_1_out);
  J_K_Flip_Flop j_k_ff_2 (.J(and_1_out), .clk(Clock), .K(and_1_out), .Q(Q1));  // open: Qn, preset, en, reset
  and and_3 (and_3_out, Q2, and_2_out);
  J_K_Flip_Flop j_k_ff_3 (.J(and_2_out), .clk(Clock), .K(and_2_out), .Q(Q2));  // open: Qn, preset, en, reset
  and and_4 (and_4_out, Q3, and_3_out);
  J_K_Flip_Flop j_k_ff_4 (.J(and_3_out), .clk(Clock), .K(and_3_out), .Q(Q3));  // open: Qn, preset, en, reset
  J_K_Flip_Flop j_k_ff_5 (.J(and_4_out), .clk(Clock), .K(and_4_out), .Q(Q4));  // open: Qn, preset, en, reset
  and and_5 (and_5_out, Q4, and_4_out);
  J_K_Flip_Flop j_k_ff_6 (.J(and_5_out), .clk(Clock), .K(and_5_out), .Q(Q5));  // open: Qn, preset, en, reset
  and and_6 (and_6_out, Q5, and_5_out);
  J_K_Flip_Flop j_k_ff_7 (.J(and_6_out), .clk(Clock), .K(and_6_out), .Q(Q7));  // open: Qn, preset, en, reset
  and and_7 (and_7_out, Q7, and_6_out);
  J_K_Flip_Flop j_k_ff_8 (.J(and_7_out), .clk(Clock), .K(and_7_out), .Q(Q7_2));  // open: Qn, preset, en, reset
endmodule

module test (
  input  Clock,
  input  Up,
  input  Down,
  output Q2,
  output Q3,
  output Q4,
  output Q5,
  output Q6,
  output Q7,
  output Q0,
  output Q1
);

  wire and_1_out, and_2_out, and_3_out, and_4_out, and_5_out, and_6_out, and_7_out, and_8_out, and_9_out,
       and_10_out, and_11_out, and_12_out, and_13_out, and_14_out, and_15_out, not_1_out, or_1_out, or_2_out,
       or_3_out, or_4_out, or_5_out, or_6_out, or_7_out, or_8_out, t_ff_1_qn, t_ff_2_qn, t_ff_3_qn,
       t_ff_4_qn, t_ff_5_qn, t_ff_6_qn, t_ff_7_qn;

  or or_1 (or_1_out, Up, and_1_out);
  not not_1 (not_1_out, Up);
  and and_1 (and_1_out, not_1_out, Down);
  T_Flip_Flop t_ff_1 (.clk(Clock), .T(or_1_out), .Q(Q0), .Qn(t_ff_1_qn));  // open: preset, reset, en
  or or_2 (or_2_out, and_2_out, and_3_out);
  and and_2 (and_2_out, Q0, Up);
  and and_3 (and_3_out, t_ff_1_qn, and_1_out);
  T_Flip_Flop t_ff_2 (.clk(Clock), .T(or_2_out), .Q(Q1), .Qn(t_ff_2_qn));  // open: preset, reset, en
  and and_4 (and_4_out, Q1, and_2_out);
  and and_5 (and_5_out, t_ff_2_qn, and_3_out);
  T_Flip_Flop t_ff_3 (.clk(Clock), .T(or_3_out), .Q(Q2), .Qn(t_ff_3_qn));  // open: preset, reset, en
  or or_3 (or_3_out, and_4_out, and_5_out);
  buf and_6 (and_6_out, Q2);  // AND_Gate
  and and_7 (and_7_out, t_ff_3_qn, and_5_out);
  or or_4 (or_4_out, and_6_out, and_7_out);
  T_Flip_Flop t_ff_4 (.clk(Clock), .T(or_4_out), .Q(Q3), .Qn(t_ff_4_qn));  // open: preset, reset, en
  and and_8 (and_8_out, Q3, and_6_out);
  and and_9 (and_9_out, t_ff_4_qn, and_7_out);
  or or_5 (or_5_out, and_8_out, and_9_out);
  T_Flip_Flop t_ff_5 (.clk(Clock), .T(or_5_out), .Q(Q4), .Qn(t_ff_5_qn));  // open: preset, reset, en
  or or_6 (or_6_out, and_10_out, and_11_out);
  buf and_10 (and_10_out, Q4);  // AND_Gate
  and and_11 (and_11_out, t_ff_5_qn, and_9_out);
  T_Flip_Flop t_ff_6 (.clk(Clock), .T(or_6_out), .Q(Q5), .Qn(t_ff_6_qn));  // open: preset, reset, en
  or or_7 (or_7_out, and_12_out, and_13_out);
  and and_12 (and_12_out, Q5, and_10_out);
  and and_13 (and_13_out, t_ff_6_qn, and_11_out);
  T_Flip_Flop t_ff_7 (.clk(Clock), .T(or_7_out), .Q(Q6), .Qn(t_ff_7_qn));  // open: preset, reset, en
  buf and_14 (and_14_out, Q6);  // AND_Gate
  and and_15 (and_15_out, t_ff_7_qn, and_13_out);
  T_Flip_Flop t_ff_8 (.clk(Clock), .T(or_8_out), .Q(Q7));  // open: Qn, preset, reset, en
  or or_8 (or_8_out, and_14_out, and_15_out);
endmodule

module Down_Counter (
  input  I0,
  input  I1,
  input  I2,
  input  I3,
  input  I4,
  input  I5,
  input  I6,
  input  I7,
  input  Clock,
  input  Clear,
  output out
);

  wire and_1_out, and_2_out, and_3_out, and_4_out, and_5_out, and_6_out, Q0, Q1, Q2, Q3, Q4, Q5, Q6, Q7,
       t_ff_1_qn, t_ff_2_qn, t_ff_3_qn, t_ff_4_qn, t_ff_5_qn, t_ff_6_qn, t_ff_7_qn;

  T_Flip_Flop t_ff_1 (.clk(Clock), .T(1'b1), .Q(Q0), .Qn(t_ff_1_qn), .preset(I0), .reset(Clear));  // open: en
  T_Flip_Flop t_ff_2 (.clk(Clock), .T(t_ff_1_qn), .Q(Q1), .Qn(t_ff_2_qn), .preset(I1), .reset(Clear));  // open: en
  and and_1 (and_1_out, t_ff_2_qn, t_ff_1_qn);
  nor nor_1 (out, Q0, Q1, Q2, Q3, Q4, Q5, Q6, Q7);
  T_Flip_Flop t_ff_3 (.clk(Clock), .T(and_1_out), .Q(Q2), .Qn(t_ff_3_qn), .preset(I2), .reset(Clear));  // open: en
  and and_2 (and_2_out, t_ff_3_qn, t_ff_2_qn, t_ff_1_qn);
  T_Flip_Flop t_ff_4 (.clk(Clock), .T(and_2_out), .Q(Q3), .Qn(t_ff_4_qn), .preset(I3), .reset(Clear));  // open: en
  and and_3 (and_3_out, t_ff_4_qn, t_ff_3_qn, t_ff_2_qn, t_ff_1_qn);
  T_Flip_Flop t_ff_5 (.clk(Clock), .T(and_3_out), .Q(Q4), .Qn(t_ff_5_qn), .preset(I4), .reset(Clear));  // open: en
  and and_4 (and_4_out, t_ff_5_qn, t_ff_4_qn, t_ff_3_qn, t_ff_2_qn, t_ff_1_qn);
  T_Flip_Flop t_ff_6 (.clk(Clock), .T(and_4_out), .Q(Q5), .Qn(t_ff_6_qn), .preset(I5), .reset(Clear));  // open: en
  and and_5 (and_5_out, t_ff_6_qn, t_ff_5_qn, t_ff_4_qn, t_ff_3_qn, t_ff_2_qn, t_ff_1_qn);
  T_Flip_Flop t_ff_7 (.clk(Clock), .T(and_5_out), .Q(Q6), .Qn(t_ff_7_qn), .preset(I6), .reset(Clear));  // open: en
  and and_6 (and_6_out, t_ff_7_qn, t_ff_6_qn, t_ff_5_qn, t_ff_4_qn, t_ff_3_qn, t_ff_2_qn, t_ff_1_qn);
  T_Flip_Flop t_ff_8 (.clk(Clock), .T(and_6_out), .Q(Q7), .preset(I7), .reset(Clear));  // open: Qn, en
endmodule

module multiply (
  input  [7:0] Q0,
  input  Clear,
  input  [7:0] Q1,
  input  Clock,
  output [7:0] out_5
);

  wire and_1_out, check, Counter_out, nor_1_out, not_1_out;
  wire [7:0] _1_to_8_bit_extender_output, Adder_s, Multiplexer_out_4;

  and and_1 (and_1_out, Clock, check);
  Down_Counter Counter (
    .Clock(and_1_out), .Clear(Clear), .I0(Q0[0]), .I1(Q0[1]), .I2(Q0[2]), .I3(Q0[3]), .I4(Q0[4]), .I5(Q0[5]),
    .I6(Q0[6]), .I7(Q0[7]), .out(Counter_out));
  not not_1 (not_1_out, nor_1_out);
  _2X8extender _1_to_8_bit_extender (.Input(not_1_out), .Output(_1_to_8_bit_extender_output));
  _2Multiplexer Multiplexer (.I0(Q1), .Selecter(_1_to_8_bit_extender_output), .out_4(Multiplexer_out_4), .I1(out_5));
  _8_bit_adder Adder (.Q0(Multiplexer_out_4), .Q1(Q1), .S(Adder_s));  // open: O
  nor nor_1 (nor_1_out, check, out_5[0], out_5[1], out_5[2], out_5[3], out_5[4], out_5[5], out_5[6], out_5[7]);
  Register register_1 (
    .Clock(and_1_out), .Clear(Clear), .Q0(Adder_s[0]), .Q1(Adder_s[1]), .Q2(Adder_s[2]), .Q3(Adder_s[3]),
    .Q4(Adder_s[4]), .Q5(Adder_s[5]), .Q6(Adder_s[6]), .Q7(Adder_s[7]), .R0(out_5[0]), .R1(out_5[1]),
    .R2(out_5[2]), .R3(out_5[3]), .R4(out_5[4]), .R5(out_5[5]), .R6(out_5[6]), .R7(out_5[7]));
  not not_2 (check, Counter_out);
endmodule

module Register (
  input  Q0,
  input  Q1,
  input  Q2,
  input  Q3,
  input  Q4,
  input  Q5,
  input  Q6,
  input  Q7,
  input  Clock,
  input  Clear,
  output R0,
  output R1,
  output R2,
  output R3,
  output R4,
  output R5,
  output R6,
  output R7
);

  D_Flip_Flop d_ff_1 (.clk(Clock), .D(Q0), .Q(R0), .reset(Clear));  // open: Qn, preset, en
  D_Flip_Flop d_ff_2 (.clk(Clock), .D(Q1), .Q(R1), .reset(Clear));  // open: Qn, preset, en
  D_Flip_Flop d_ff_3 (.clk(Clock), .D(Q2), .Q(R2), .reset(Clear));  // open: Qn, preset, en
  D_Flip_Flop d_ff_4 (.clk(Clock), .D(Q3), .Q(R3), .reset(Clear));  // open: Qn, preset, en
  D_Flip_Flop d_ff_5 (.clk(Clock), .D(Q4), .Q(R4), .reset(Clear));  // open: Qn, preset, en
  D_Flip_Flop d_ff_6 (.clk(Clock), .D(Q5), .Q(R5), .reset(Clear));  // open: Qn, preset, en
  D_Flip_Flop d_ff_7 (.clk(Clock), .D(Q6), .Q(R6), .reset(Clear));  // open: Qn, preset, en
  D_Flip_Flop d_ff_8 (.clk(Clock), .D(Q7), .Q(R7), .reset(Clear));  // open: Qn, preset, en
endmodule

module _2Multiplexer (
  input  [7:0] I0,
  input  [7:0] Selecter,
  input  [7:0] I1,
  output [7:0] out_4
);

  wire [7:0] and_1_out, and_2_out, not_1_out;

  assign not_1_out = ~Selecter;  // NOT_Gate not_1, 8 bits wide
  assign and_1_out = I0 & not_1_out;  // AND_Gate and_1, 8 bits wide
  assign and_2_out = Selecter & I1;  // AND_Gate and_2, 8 bits wide
  assign out_4 = and_1_out | and_2_out;  // OR_Gate or_1, 8 bits wide
endmodule

module J_K_flip_flop (
  input  J,
  input  C,
  input  K,
  output Q,
  output nQ
);

  wire nand_1_out, nand_2_out;

  nand nand_1 (nand_1_out, J, nQ, C);
  nand nand_2 (nand_2_out, C, Q, K);
  nand nand_3 (Q, nand_1_out, nQ);
  nand nand_4 (nQ, Q, nand_2_out);

  // Notes on the sheet:
  //   J K flip flop
endmodule

module ALU (
);

  wire [7:0] MultiPlexer_2_out_4, MultiPlexer_3_out_4, MultiPlexer_4_out_4, MultiPlexer_out_4, undriven,
       undriven_2, undriven_3, undriven_4, undriven_5, undriven_6, undriven_7;

  _2Multiplexer MultiPlexer (.I0(undriven_3), .out_4(MultiPlexer_out_4), .I1(undriven_2));  // open: Selecter
  _2Multiplexer MultiPlexer_2 (.I0(undriven_5), .out_4(MultiPlexer_2_out_4), .I1(undriven_4));  // open: Selecter
  _2Multiplexer MultiPlexer_3 (.I0(undriven_7), .out_4(MultiPlexer_3_out_4), .I1(undriven_6));  // open: Selecter
  _2Multiplexer MultiPlexer_4 (.out_4(MultiPlexer_4_out_4), .I1(undriven));  // open: I0, Selecter
  _2Multiplexer MultiPlexer_5 (.I0(MultiPlexer_2_out_4), .I1(MultiPlexer_out_4));  // open: Selecter, out_4
  _2Multiplexer MultiPlexer_6 (.I0(MultiPlexer_4_out_4), .I1(MultiPlexer_3_out_4));  // open: Selecter, out_4
  multiply Multiplier ();  // open: Q0, Clear, Q1, Clock, out_5
  _8_bit_adder Adder ();  // open: Q0, Q1, S, O
  // AND_Gate and_1 is placed but not wired
  // OR_Gate or_1 is placed but not wired
endmodule

module test2 (
  input  Set,
  input  Q3,
  input  Q4,
  input  Q5,
  input  Q7,
  input  Q6,
  input  Q2,
  input  Q1,
  input  Q0,
  input  Mode,
  input  Clock,
  input  Clear,
  output out
);

  wire and_1_out, and_3_out, and_4_out, and_6_out, and_7_out, and_9_out, and_10_out, and_12_out, and_13_out,
       and_15_out, and_16_out, and_18_out, and_19_out, and_21_out, and_22_out, and_24_out, j_k_ff_1_q,
       j_k_ff_1_qn, j_k_ff_2_q, j_k_ff_2_qn, j_k_ff_3_q, j_k_ff_3_qn, j_k_ff_4_q, j_k_ff_4_qn, j_k_ff_5_q,
       j_k_ff_5_qn, j_k_ff_6_q, j_k_ff_6_qn, j_k_ff_7_q, j_k_ff_7_qn, j_k_ff_8_q, j_k_ff_8_qn, not_1_out,
       or_1_out, or_2_out, or_3_out, or_4_out, or_5_out, or_6_out, or_7_out, Q0_t, Q1_t, Q2_t, Q3_t, Q4_t,
       Q5_t, Q6_t, Q7_t;

  and and_1 (and_1_out, Set, Q0);
  J_K_Flip_Flop j_k_ff_1 (
    .J(1'b1), .clk(Clock), .K(1'b1), .Q(j_k_ff_1_q), .Qn(j_k_ff_1_qn), .preset(and_1_out), .reset(Clear));  // open: en
  not not_1 (not_1_out, Mode);
  and and_2 (Q0_t, Mode, j_k_ff_1_q);
  and and_3 (and_3_out, j_k_ff_1_qn, not_1_out);
  and and_4 (and_4_out, Set, Q1);
  or or_1 (or_1_out, Q0_t, and_3_out);
  and and_5 (Q1_t, Q0_t, j_k_ff_2_q);
  J_K_Flip_Flop j_k_ff_2 (
    .J(or_1_out), .clk(Clock), .K(or_1_out), .Q(j_k_ff_2_q), .Qn(j_k_ff_2_qn), .preset(and_4_out),
    .reset(Clear));  // open: en
  and and_6 (and_6_out, j_k_ff_2_qn, and_3_out);
  or or_2 (or_2_out, Q1_t, and_6_out);
  and and_7 (and_7_out, Set, Q2);
  J_K_Flip_Flop j_k_ff_3 (
    .J(or_2_out), .clk(Clock), .K(or_2_out), .Q(j_k_ff_3_q), .Qn(j_k_ff_3_qn), .preset(and_7_out),
    .reset(Clear));  // open: en
  and and_8 (Q2_t, Q1_t, j_k_ff_3_q);
  or or_3 (or_3_out, Q2_t, and_9_out);
  and and_9 (and_9_out, j_k_ff_3_qn, and_6_out);
  and and_10 (and_10_out, Set, Q3);
  J_K_Flip_Flop j_k_ff_4 (
    .J(or_3_out), .clk(Clock), .K(or_3_out), .Q(j_k_ff_4_q), .Qn(j_k_ff_4_qn), .preset(and_10_out),
    .reset(Clear));  // open: en
  and and_11 (Q3_t, Q2_t, j_k_ff_4_q);
  and and_12 (and_12_out, j_k_ff_4_qn, and_9_out);
  and and_13 (and_13_out, Set, Q4);
  or or_4 (or_4_out, Q3_t, and_12_out);
  and and_14 (Q4_t, Q3_t, j_k_ff_5_q);
  J_K_Flip_Flop j_k_ff_5 (
    .J(or_4_out), .clk(Clock), .K(or_4_out), .Q(j_k_ff_5_q), .Qn(j_k_ff_5_qn), .preset(and_13_out),
    .reset(Clear));  // open: en
  and and_15 (and_15_out, j_k_ff_5_qn, and_12_out);
  or or_5 (or_5_out, Q4_t, and_15_out);
  and and_16 (and_16_out, Set, Q5);
  J_K_Flip_Flop j_k_ff_6 (
    .J(or_5_out), .clk(Clock), .K(or_5_out), .Q(j_k_ff_6_q), .Qn(j_k_ff_6_qn), .preset(and_16_out),
    .reset(Clear));  // open: en
  nor nor_1 (out, Q0_t, Q1_t, Q2_t, Q3_t, Q4_t, Q5_t, Q6_t, Q7_t);
  and and_17 (Q5_t, Q4_t, j_k_ff_6_q);
  and and_18 (and_18_out, j_k_ff_6_qn, and_15_out);
  and and_19 (and_19_out, Set, Q6);
  or or_6 (or_6_out, Q5_t, and_18_out);
  and and_20 (Q6_t, Q5_t, j_k_ff_7_q);
  J_K_Flip_Flop j_k_ff_7 (
    .J(or_6_out), .clk(Clock), .K(or_6_out), .Q(j_k_ff_7_q), .Qn(j_k_ff_7_qn), .preset(and_19_out),
    .reset(Clear));  // open: en
  and and_21 (and_21_out, j_k_ff_7_qn, and_18_out);
  or or_7 (or_7_out, Q6_t, and_21_out);
  and and_22 (and_22_out, Set, Q7);
  J_K_Flip_Flop j_k_ff_8 (
    .J(or_7_out), .clk(Clock), .K(or_7_out), .Q(j_k_ff_8_q), .Qn(j_k_ff_8_qn), .preset(and_22_out),
    .reset(Clear));  // open: en
  and and_23 (Q7_t, Q6_t, j_k_ff_8_q);
  and and_24 (and_24_out, j_k_ff_8_qn, and_21_out);
  // OR_Gate or_8 has open pins: in0=Q7_t, in1=and_24_out, out=open
endmodule

module _2X8extender (
  input  Input,
  output [7:0] Output
);


  assign Output = {8{Input}};

  // Other names for the same wires on the sheet: I = Input
endmodule

module _2_s_complement (
  input  [7:0] in,
  output [7:0] out,
  output overflow
);

  wire [0:0] not_1_out;
  wire [7:0] not_2_out;

  not not_1 (not_1_out[0], 1'b0);
  assign not_2_out = ~in;  // NOT_Gate not_2, 8 bits wide
  _8_bit_adder u_8_bit_adder_1 (.Q0(not_2_out), .Q1({{7{1'b0}}, not_1_out[0]}), .S(out), .O(overflow));
endmodule

module subtractor (
  input  [7:0] A,
  input  [7:0] B,
  output [7:0] OUT,
  output Overflow_adder,
  output Overflow_Complement
);

  wire [7:0] n2_s_complement_1_out;

  _2_s_complement u_2_s_complement_1 (.in(B), .out(n2_s_complement_1_out), .overflow(Overflow_Complement));
  _8_bit_adder u_8_bit_adder_1 (.Q0(A), .Q1(n2_s_complement_1_out), .S(OUT), .O(Overflow_adder));
endmodule

module counter (
  input  counter,
  input  clear,
  output [7:0] out_3
);

  up_counter up_counter_1 (
    .Clock(counter), .Clear(clear), .I0(1'b0), .I1(1'b0), .I2(1'b0), .I3(1'b0), .I4(1'b0), .I5(1'b0),
    .I6(1'b0), .I7(1'b0), .out(out_3));
endmodule

module up_counter (
  input  I0,
  input  I1,
  input  I2,
  input  I3,
  input  I4,
  input  I5,
  input  I6,
  input  I7,
  input  Clock,
  input  Clear,
  output [7:0] out
);

  wire and_1_out, and_2_out, and_3_out, and_4_out, and_5_out, and_6_out;

  T_Flip_Flop t_ff_1 (.clk(Clock), .T(1'b1), .Q(out[0]), .preset(I0), .reset(Clear));  // open: Qn, en
  T_Flip_Flop t_ff_2 (.clk(Clock), .T(out[0]), .Q(out[1]), .preset(I1), .reset(Clear));  // open: Qn, en
  and and_1 (and_1_out, out[0], out[1]);
  T_Flip_Flop t_ff_3 (.clk(Clock), .T(and_1_out), .Q(out[2]), .preset(I2), .reset(Clear));  // open: Qn, en
  and and_2 (and_2_out, out[0], out[1], out[2]);
  T_Flip_Flop t_ff_4 (.clk(Clock), .T(and_2_out), .Q(out[3]), .preset(I3), .reset(Clear));  // open: Qn, en
  and and_3 (and_3_out, out[0], out[1], out[2], out[3]);
  T_Flip_Flop t_ff_5 (.clk(Clock), .T(and_3_out), .Q(out[4]), .preset(I4), .reset(Clear));  // open: Qn, en
  and and_4 (and_4_out, out[0], out[1], out[2], out[3], out[4]);
  T_Flip_Flop t_ff_6 (.clk(Clock), .T(and_4_out), .Q(out[5]), .preset(I5), .reset(Clear));  // open: Qn, en
  and and_5 (and_5_out, out[0], out[1], out[2], out[3], out[4], out[5]);
  T_Flip_Flop t_ff_7 (.clk(Clock), .T(and_5_out), .Q(out[6]), .preset(I6), .reset(Clear));  // open: Qn, en
  and and_6 (and_6_out, out[0], out[1], out[2], out[3], out[4], out[5], out[6]);
  T_Flip_Flop t_ff_8 (.clk(Clock), .T(and_6_out), .Q(out[7]), .preset(I7), .reset(Clear));  // open: Qn, en

  // Other names for the same wires on the sheet: Q0 = out[0]; Q1 = out[1]; Q2 = out[2]; Q3 = out[3]; Q4 = out[4];
  //   Q5 = out[5]; Q6 = out[6]; Q7 = out[7]
endmodule

module dividor (
  input  [7:0] in_1,
  input  [7:0] in_2
);

  wire n2_s_complement_2_overflow, undriven;
  wire [7:0] n2_s_complement_1_out, n2multiplexer_1_out_4, n2x8extender_1_output, n8_bit_adder_1_s,
       register_1_r0;

  _2Multiplexer u_2multiplexer_1 (
    .I0(register_1_r0), .Selecter(n2x8extender_1_output), .out_4(n2multiplexer_1_out_4),
    .I1(n2_s_complement_1_out));
  _2_s_complement u_2_s_complement_1 (.in(in_2), .out(n2_s_complement_1_out));  // open: overflow
  _8_bit_adder u_8_bit_adder_1 (.Q0(in_1), .Q1(n2multiplexer_1_out_4), .S(n8_bit_adder_1_s));  // open: O
  _2X8extender u_2x8extender_1 (.Input(n2_s_complement_2_overflow), .Output(n2x8extender_1_output));
  Register register_1 (
    .Clear(undriven), .Q0(n8_bit_adder_1_s[0]), .Q1(n8_bit_adder_1_s[1]), .Q2(n8_bit_adder_1_s[2]),
    .Q3(n8_bit_adder_1_s[3]), .Q4(n8_bit_adder_1_s[4]), .Q5(n8_bit_adder_1_s[5]), .Q6(n8_bit_adder_1_s[6]),
    .Q7(n8_bit_adder_1_s[7]), .R0(register_1_r0[0]), .R1(register_1_r0[1]), .R2(register_1_r0[2]),
    .R3(register_1_r0[3]), .R4(register_1_r0[4]), .R5(register_1_r0[5]), .R6(register_1_r0[6]),
    .R7(register_1_r0[7]));  // open: Clock
  _2_s_complement u_2_s_complement_2 (.in(register_1_r0), .overflow(n2_s_complement_2_overflow));  // open: out
  counter counter_1 ();  // open: counter, clear, out_3
endmodule
